# Fritzing sketch v01.00.00 (saved by Fritzing 0.9.10b)
breadboards: 1

parts:
  Part1 = Arduino Mega 2560 (Rev3)
  S1 = Pushbutton [package="[THT]"]
  R3 = Resistor [tolerance=±5% resistance=220 power=0.25 package=THT]
  J1 = female pin header, 2 pins [form="♀ (female)"]
  LCD2 = LCD screen
  R4 = Resistor [tolerance=±5% resistance=226 power=0.25 package=THT]
  Part3 = Adafruit MPRLS Sensor Breakout [part_number=3965]
  S2 = Pushbutton [package="[THT]"]
  S3 = Pushbutton [package="[THT]"]
  R9 = Trimmer Potentiometer [maximum_resistance=10kΩ knob_status=50% power=0.5W package=THT]
  LED3 = LED - 5mm [color="Red (633nm)" current=0.030 package="5 mm [THT]"]

nets:
  N1: Part1.A15, R9.wiper
  N2: Part1.D21/SCL, Part3.SCL
  N3: Part1.D20/SDA, Part3.SDA
  N4: Part1.D13_PWM, S1.Pin_3, S1.Pin_4
  N5: Part1.D12_PWM, LCD2.RS
  N6: Part1.D11_PWM, LCD2.E
  N7: Part1.RESET, S2.Pin_3, S2.Pin_4
  3V3: Part1.3V3, Part3.3.3V
  GND: Part1.GND, LCD2.VSS, LCD2.R/W, LCD2.LED-
  N8: Part1.D2_PWM, LCD2.DB7
  N9: Part1.D3_PWM, LCD2.DB6
  N10: Part1.D4_PWM, LCD2.DB5
  N11: Part1.D5_PWM, LCD2.DB4
  N12: Part1.D6_PWM, LCD2.V0
  N13: Part1.D7_PWM, S3.Pin_3, S3.Pin_4
  N14: Part1.D22, R3.Pin_0
  N15: Part1.D26, J1.pin1
  N16: S1.Pin_1, S1.Pin_2, J1.pin2, Part3.GND, S3.Pin_1, S3.Pin_2, R9.leg2, LED3.cathode
  N17: R3.Pin_1, LED3.anode
  N18: LCD2.VDD, R4.Pin_1
  N19: LCD2.LED+, R4.Pin_0
  N20: S2.Pin_1, S2.Pin_2

notes:
  Digital Loggers Inc IoT Relay
  OK / MANUAL
  RESET / RESTART
  NO LIMITS

custom parts:
  Adafruit MPRLS Sensor Breakout: This pressure sensor is special because it comes with a metal port - you can easily attach a tube to it, to measure air pressure inside a close space. In particular we think this would be a great sensor for use with making DIY assistive tech "Sip & Puff" interfaces, or measuring the pressure within a vacuum chamber or other pressurized container. The port is made of stainless steel and is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

// code stored in the sketch: v01.00.00.ino
#include <Arduino.h>


/*!
 * @file mprls_simpletest.ino
 *
 * A basic test of the sensor with default settings
 * 
 * Designed specifically to work with the MPRLS sensor from Adafruit
 * ----> https://www.adafruit.com/products/3965
 *
 * These sensors use I2C to communicate, 2 pins (SCL+SDA) are required
 * to interface with the breakout.
 *
 * Adafruit invests time and resources providing this open source code,
 * please support Adafruit and open-source hardware by purchasing
 * products from Adafruit!
 *
 * Written by Limor Fried/Ladyada for Adafruit Industries.  
 *
 * MIT license, all text here must be included in any redistribution.
 * 
 * Code is based on the above, with added functionality for an override button,
 * and an LED indicator
 * 
 */


 /*
  * 1 Bar = 14.61 PSI
  * -0.25 Bar = (1-0.25) = 0.75 Bar = 10.88 PSI
  * Sources : https://www.gflow.fr/upload/files/psi-bar.pdf and http://dominique.melotti.pagesperso-orange.fr/bar.htm
  * 1 Bar = 1000 Hectopascals
  * 0.75 Bar = 750 hPa
  * Source : https://convertlive.com/fr/u/convert/barres/a/hectopascals#0.75
  * -0.25 Bar = 850 hPa = +0.75 Bar
  */
 
#include <Wire.h>
#include <Adafruit_MPRLS.h>
#include <LiquidCrystal.h>


// You dont *need* a reset and EOC pin for most uses, so we set to -1 and don't connect
#define RESET_PIN  -1  // set to any GPIO pin # to hard-reset on begin()
#define EOC_PIN    -1  // set to any GPIO pin to read end-of-conversion by pin
Adafruit_MPRLS mpr = Adafruit_MPRLS(RESET_PIN, EOC_PIN);


// Pin Settings
const int ledPin =  22;
const int buttonPin = 13;
const int relayPin = 26;
const int contrastPin = 6;
const int potentiometerPin = A15;
const int buttonFPin = 7;


// SET THE PRESSURE HERE (In absolute Bar)
float triggerPressure = 1.01;  // In ABS - Default is 0.825 (-0.175 bar)
float lowPoint = 0.85;         // In ABS - Default is 0.750 (-0.250 bar)


// BUTTOM
// The button take effect between the lowPoint and the triggerPressur for restart the vacuum until the the lowPoint.
int buttonState = 0;
int buttonFState = 0;
String state;
float potentiometerValue;


// Settings for the LCD:
const int rs = 12, en = 11, d4 = 5, d5 = 4, d6 = 3, d7 = 2;
LiquidCrystal lcd(rs, en, d4, d5, d6, d7);
int Contrast=75;


// Settings for initialisation
int EOI = 0;
int Stop;



void setup() {
  Serial.begin(115200);
  analogWrite(contrastPin,Contrast);
  Serial.println("MPRLS Simple Test");
  lcd.begin(16, 2);
  if (! mpr.begin()) {
    Serial.println("Failed to communicate with MPRLS sensor, check wiring?");
    while (1) {
      delay(10);
    }
  }
  Serial.println("Found MPRLS sensor");


  // initialize the LED pin as an output:
  pinMode(ledPin, OUTPUT);
  pinMode(relayPin, OUTPUT);
  pinMode(buttonPin, INPUT_PULLUP);
  pinMode(buttonFPin, INPUT_PULLUP); // Bouton est passant en PULLUP


  // Forced work (only at the startup or after RESET)
  buttonFState = digitalRead(buttonFPin);
  Serial.print("Etat du bouton de marche forc�e : "); Serial.println(buttonFState);
  if (buttonFState == 0) { // Infinite loop
    Serial.println();
    Serial.println("*****************");
    Serial.println("**** WARNING ****");
    Serial.println("*****************");
    Serial.println();
    while (1) {
      float pressure_hPa = mpr.readPressure();
      digitalWrite(ledPin, HIGH);
      digitalWrite(relayPin, HIGH);
      state = "on";
      Serial.print("Pressure (hPa): "); Serial.println(String(pressure_hPa));
      Serial.println("FORCED WORK ! BE CAREFULL !!!");
      lcd.clear();
      lcd.print(" NO LIMITS !!!! ");
      lcd.setCursor(0, 1);
      lcd.print("RESET TO STOP IT");
      delay (1000);
    }
  }



  // INITIALISATION
  lcd.clear();
  lcd.print(" INITIALISATION");
  lcd.setCursor(0, 1);
  lcd.print("****************");
  Serial.print("buttonState : "); Serial.println(String(buttonState));
  Serial.print("potentiometerValue : "); Serial.println(analogRead(A15));
  Serial.println();
  delay(2000);


}



void loop() {



// Adjust the trigger and low points
while (EOI != 2) { // Condition � v�rifier pour rester dans la boucle jusqu'� ce que...
  if (EOI == 0) {
    // Setting the Low point
    buttonState = digitalRead(buttonPin);
    lcd.clear();
    lcd.print("SET low point :");
    lcd.setCursor(0, 1);
    potentiometerValue = (analogRead(potentiometerPin) * (-0.33/1024));
    lcd.print(potentiometerValue); lcd.print(" bar");


    // Condition de sortie du WHILE
    if (buttonState == LOW) {
      EOI = 1;
      lowPoint = 1 + potentiometerValue;
    }
    Serial.print("buttonState : "); Serial.println(String(buttonState)); 
    Serial.print("EOI : "); Serial.println(String(EOI));
    Serial.print("lowPoint : "); Serial.print(String(lowPoint)); Serial.println(" bar (Absolut) by DEFAULT");
    Serial.println();
    delay(400); 
  } else {
    if (EOI == 1) {
      // Settings the Trigger point
      buttonState = digitalRead(buttonPin);
      lcd.clear();
      lcd.print("SET trigger pt :");
      lcd.setCursor(0, 1);
      potentiometerValue = (analogRead(potentiometerPin) * (-0.23/1024));
      lcd.print(potentiometerValue); lcd.print(" bar");
      
      // Condition de sortie du WHILE
      if (buttonState == LOW) {
        EOI = 2;
        triggerPressure = 1 + potentiometerValue;
      }
      Serial.print("buttonState : "); Serial.println(String(buttonState)); 
      Serial.print("EOI : "); Serial.println(String(EOI));
      Serial.print("lowPoint : "); Serial.print(String(lowPoint)); Serial.println(" bar (Absolut) REGISTRED");
      Serial.print("triggerPressure : "); Serial.print(String(triggerPressure)); Serial.println(" bar (Absolut) by DEFAULT");
      Serial.println();
      delay(400);
    }
  }
}



/*
*  We're going to need to read the pressure, and then decide if we need to trigger the relay for the vacuum
*  once we trigger the vacuum, we want to check the pressure every second until it hits the expected pressure,
*  once it goes above the preferred pressure, it will close the relay again.
*
*  Beetwen the lowPoint and the triggerPressure, the vaccum system can be restarted if the "OK - RESTART" button is pressed. 
*/


lcd.clear();
lcd.print("LET'S STARTED !!");
delay(2500);
lcd.clear();


while (1) { // Infinite loop
  lcd.print("Cur Bar:");
  lcd.setCursor(0, 1);
  lcd.print("Cur hPa:"); 


  buttonState = digitalRead(buttonPin);
  float pressure_hPa = mpr.readPressure();
  Serial.print("Pressure (hPa): "); Serial.println(String(pressure_hPa));
  float pressureBar = pressure_hPa / 1000;
  Serial.print("Pressure (Bar): "); Serial.println(String(pressureBar));
  Serial.print("Light is : "); Serial.println(state);
  Serial.print("lowPoint : "); Serial.print(String(lowPoint)); Serial.println(" bar (Absolut) REGISTRED");
  Serial.print("triggerPressure : "); Serial.print(String(triggerPressure)); Serial.println(" bar (Absolut) REGISTRED");
  Serial.println();
  lcd.setCursor(9, 0);
  lcd.print(String(pressureBar));
  lcd.setCursor(9, 1);
  lcd.print(String(pressure_hPa));
  if (buttonState == HIGH) {    // Normally must be true everytime
    if (pressureBar >= triggerPressure) {
      // Turn on the LED to indicate we're going to flip on the vacuum
      digitalWrite(ledPin, HIGH);
      digitalWrite(relayPin, HIGH);
      state = "on";
    } else if (pressureBar <= lowPoint) {
      // Turn off the LED and relay
      digitalWrite(ledPin, LOW);
      digitalWrite(relayPin, LOW);
      state = "off";
    } /*else {
      digitalWrite(ledPin, LOW);
      digitalWrite(relayPin, LOW);
      state = "off";
    }*/
  } else if (buttonState == HIGH) {
    digitalWrite(ledPin, LOW);
    digitalWrite(relayPin, LOW);
    state = "off";
  } else {
    digitalWrite(ledPin, HIGH);
    digitalWrite(relayPin, HIGH);
    state = "on";
  }
  delay(1000);
  }


}

// code stored in the sketch: v01.10.00.ino
#include <Arduino.h>
#include <Wire.h>
#include <Adafruit_MPRLS.h>
#include <LiquidCrystal.h>


// You dont *need* a reset and EOC pin for most uses, so we set to -1 and don't connect
#define RESET_PIN  -1  // set to any GPIO pin # to hard-reset on begin()
#define EOC_PIN    -1  // set to any GPIO pin to read end-of-conversion by pin
Adafruit_MPRLS mpr = Adafruit_MPRLS(RESET_PIN, EOC_PIN);


// Definition des Pin;
const int LedAction =  22;
const int RelayMoteur = 24;
const int ButtonValidation = 26;
const int ButtonForcer = 28;
const int PinPotentio = A15;
const int PinPotentio2 = A14;

//configuration des Seuils Mini / Maxi;

float highPoint = -0.175;  // In ABS - Default is 0.825 (-0.175 bar)
float lowPoint = -0.250;         // In ABS - Default is 0.750 (-0.250 bar)
float Pression = mpr.readPressure()/1000;

//Initialisation de l'etats des Bouttons;

int ButtonValidation = 0;
float Valeurpotentio;
float Valeurpotentio2;

// Parametre LCD ;
const int rs = 12, en = 11, d4 = 5, d5 = 4, d6 = 3, d7 = 2;
LiquidCrystal lcd(rs, en, d4, d5, d6, d7);
const int contrastPin = 6;
int Contrast=75;    // Contraste de 0 à 100


// Settings for initialisation
int StateConfig = 0;
int Stop;

void Forcer()
  {
    Serial.print("Etat du bouton de marche forcer: ");
    lcd.clear();
    lcd.setCursor(0, 0);
    lcd.print(" Marche Forcer ");

      do
        {
          digitalWrite(LedAction, HIGH);
          digitalWrite(RelayMoteur, HIGH);
          lcd.setCursor(0, 1);
          lcd.print(Pression);lcd.println(" Bar");
        }
      while (digitalRead(ButtonForcer==LOW));
  }



void setup() 
  {
    Serial.begin(115200);
    analogWrite(contrastPin,Contrast);
    Serial.println("MPRLS Simple Test");
    lcd.begin(16, 2);
    lcd.print("Hello");
    if (! mpr.begin(0x18)) 

      {

        Serial.println("Failed to communicate with MPRLS sensor, check wiring?");
        lcd.print("Error Com MPRLS");
        while (1) 

      {
      
      delay(10);
    }
  }
  Serial.println("Found MPRLS sensor");
  lcd.print("Setup OK");
  delay(1000);


  // INITIALISATION
  lcd.clear();
  lcd.print("INITIALISATION");
  lcd.setCursor(0, 1);
  lcd.print("****************");
  //Serial.print("buttonState : "); Serial.println(String(buttonState));
  //Serial.print("potentiometerValue : "); Serial.println(analogRead(A15));
  //Serial.println();
  delay(2000);


  // initialize the LED pin as an output:
  pinMode(LedAction, OUTPUT);
  pinMode(RelayMoteur, OUTPUT);
  pinMode(ButtonValidation, INPUT_PULLUP);
  pinMode(ButtonForcer, INPUT_PULLUP); // Bouton est passant en PULLUP
  attachInterrupt(digitalPinToInterrupt(ButtonForcer), Forcer, FALLING);


void loop() 
{  
  if (StateConfig == 0){Mini()};
  Auto();     
}




void Mini()
  {
    do
      {
        lcd.clear();
        lcd.print("SET low point :");
        lcd.setCursor(0, 1);
        Valeurpotentio = (analogRead(PinPotentio) * (-0.33/1024));
        lcd.print(Valeurpotentio); lcd.print(" bar");
      }
    while(buttonState == LOW);  
    StateConfig=1;
    lowPoint = 1 + Valeurpotentio;
    Maxi();

  }


void Maxi()
  {
    do
      {
        lcd.clear();
        lcd.print("SET High point :");
        lcd.setCursor(0, 1);
        Valeurpotentio2 = (analogRead(PinPotentio2) * (-0.33/1024));
        lcd.print(Valeurpotentio2); lcd.print(" bar");
      }
    while(buttonState == LOW);  
    StateConfig=2;
    highPoint = 1 + Valeurpotentio2;

  }


void Auto() 
  {
    lcd.clear();
    lcd.print("LET'S STARTED !!");
    delay(2500);
    lcd.clear();


      while (1) 
        { // Infinite loop
          lcd.print("Cur Bar:");
          lcd.setCursor(0, 1);
          lcd.setCursor(9, 0);
          lcd.print(String(Pression));

                  //Serial.print("Pressure (hPa): "); Serial.println(String(pressure_hPa));
                  //float pressureBar = pressure_hPa / 1000;
                  //Serial.print("Pressure (Bar): "); Serial.println(String(pressureBar));
                  //Serial.print("Light is : "); Serial.println(state);
                  //Serial.print("lowPoint : "); Serial.print(String(lowPoint)); Serial.println(" bar (Absolut) REGISTRED");
                  //Serial.print("triggerPressure : "); Serial.print(String(triggerPressure)); Serial.println(" bar (Absolut) REGISTRED");
                  //Serial.println();
                  
          If (DigitalRead(ButtonForcer==LOW)) {Forcer();}

          if (Pression <= highpoint)   // Turn on the LED to indicate we're going to flip on the vacuum
            {
              digitalWrite(LedAction, HIGH);
              digitalWrite(RelayMoteur, HIGH);
            }

          else if (pression >= lowPoint) // Turn off the LED and relay
            {
              digitalWrite(LedAction, LOW);
              digitalWrite(RelayMoteur, LOW);
            }
        }
  }

// code stored in the sketch: v01.20.00.ino
#include <Arduino.h>
#include <Wire.h>
#include <Adafruit_MPRLS.h>
#include <LiquidCrystal.h>


// Vous n'avez PAS besoin de pin RESET ni EOC dans la plus part des cas. Donc ces fonctions sont définies à -1 et ne sont pas utilisées.
#define RESET_PIN  -1  // Pour définir n'importe quelle broche # du GPIO comme un hard-reset au démarrage begin()
#define EOC_PIN    -1  // Pour définir n'importe quelle broche du GPIO comme une attente delecture pour end-of-conversion
// Adresse I2C du capteur MPRLS begin(0x18)
Adafruit_MPRLS mpr = Adafruit_MPRLS(RESET_PIN, EOC_PIN);


// Attribution des broches
const int ledPin =  22;
const int buttonPin = 13;
const int relayPin = 26;
const int contrastPin = 6;
const int potentiometerPin = A15;
const int buttonFPin = 7;


// Définition des pression (En ABSOLU - Bar)
// Pour triggerPressure, par défaut, en relatif est de -0.175 bar soit 0.825 bar ABS
// Pour lowPoint, par défaut, en relatif est de -0.250 bar soit 0.750 bar ABS
// Pour un potentiomère unique ET commun, les valeurs par défaut seront de :
float lowPoint = 0.85;         // 0.85
float triggerPressure = 1.01;  // 1.01



// Boutons
// The button take effect between the lowPoint and the triggerPressur for restart the vacuum until the the lowPoint.
int buttonState = 0;
int buttonFState = 0;
String state;
float potentiometerValue;


// Settings for the LCD:
const int rs = 12, en = 11, d4 = 5, d5 = 4, d6 = 3, d7 = 2;
LiquidCrystal lcd(rs, en, d4, d5, d6, d7);
int Contrast=75;


// Settings for initialisation
int EOI = 0;
int Stop;



void setup() {
  Serial.begin(115200);
  analogWrite(contrastPin,Contrast);
  Serial.println("Test du capteur MPRLS");
  lcd.begin(16, 2);
  if (! mpr.begin(0x18)) {
    Serial.println("Communication impossible. Vérifiez le branchement et/ou l'adresse.");
    while (1) {
      delay(10);
    }
  }
  Serial.println("Capteur MPRLS fonctionnel.");


  // initialize the LED pin as an output:
  pinMode(ledPin, OUTPUT);
  pinMode(relayPin, OUTPUT);
  pinMode(buttonPin, INPUT_PULLUP);
  pinMode(buttonFPin, INPUT_PULLUP); // Bouton est passant en PULLUP


  // Forced work (only at the startup or after RESET)
  buttonFState = digitalRead(buttonFPin);
  Serial.print("Etat du bouton de marche forcée : "); Serial.println(buttonFState);
  if (buttonFState == 0) { // Infinite loop
    Serial.println();
    Serial.println("*****************");
    Serial.println("**** WARNING ****");
    Serial.println("*****************");
    Serial.println();
    while (1) {
      float pressure_hPa = mpr.readPressure();
      digitalWrite(ledPin, HIGH);
      digitalWrite(relayPin, HIGH);
      state = "on";
      Serial.print("Pressure (hPa): "); Serial.println(String(pressure_hPa));
      Serial.println("FORCED WORK ! BE CAREFULL !!!");
      lcd.clear();
      lcd.print(" NO LIMITS !!!! ");
      lcd.setCursor(0, 1);
      lcd.print("RESET TO STOP IT");
      delay (1000);
    }
  }



  // INITIALISATION
  lcd.clear();
  lcd.print(" INITIALISATION");
  lcd.setCursor(0, 1);
  lcd.print("****************");
  Serial.print("buttonState : "); Serial.println(String(buttonState));
  Serial.print("potentiometerValue : "); Serial.println(analogRead(A15));
  Serial.println();
  delay(2000);


}



void loop() {



// Adjust the trigger and low points
while (EOI != 2) { // Condition à vérifier pour rester dans la boucle jusqu'à ce que...
  if (EOI == 0) {
    // Setting the Low point
    buttonState = digitalRead(buttonPin);
    lcd.clear();
    lcd.print("SET low point :");
    lcd.setCursor(0, 1);
    potentiometerValue = (analogRead(potentiometerPin) * (-0.33/1024));
    lcd.print(potentiometerValue); lcd.print(" bar");


    // Condition de sortie du WHILE
    if (buttonState == LOW) {
      EOI = 1;
      lowPoint = 1 + potentiometerValue;
    }
    Serial.print("buttonState : "); Serial.println(String(buttonState)); 
    Serial.print("EOI : "); Serial.println(String(EOI));
    Serial.print("lowPoint : "); Serial.print(String(lowPoint)); Serial.println(" bar (Absolut) by DEFAULT");
    Serial.println();
    delay(400); 
  } else {
    if (EOI == 1) {
      // Settings the Trigger point
      buttonState = digitalRead(buttonPin);
      lcd.clear();
      lcd.print("SET trigger pt :");
      lcd.setCursor(0, 1);
      potentiometerValue = (analogRead(potentiometerPin) * (-0.23/1024));
      lcd.print(potentiometerValue); lcd.print(" bar");
      
      // Condition de sortie du WHILE
      if (buttonState == LOW) {
        EOI = 2;
        triggerPressure = 1 + potentiometerValue;
      }
      Serial.print("buttonState : "); Serial.println(String(buttonState)); 
      Serial.print("EOI : "); Serial.println(String(EOI));
      Serial.print("lowPoint : "); Serial.print(String(lowPoint)); Serial.println(" bar (Absolut) REGISTRED");
      Serial.print("triggerPressure : "); Serial.print(String(triggerPressure)); Serial.println(" bar (Absolut) by DEFAULT");
      Serial.println();
      delay(400);
    }
  }
}



/*
*  We're going to need to read the pressure, and then decide if we need to trigger the relay for the vacuum
*  once we trigger the vacuum, we want to check the pressure every second until it hits the expected pressure,
*  once it goes above the preferred pressure, it will close the relay again.
*
*  Beetwen the lowPoint and the triggerPressure, the vaccum system can be restarted if the "OK - RESTART" button is pressed. 
*/


lcd.clear();
lcd.print("LET'S STARTED !!");
delay(2500);
lcd.clear();


while (1) { // Infinite loop
  lcd.print("Cur Bar:");
  lcd.setCursor(0, 1);
  lcd.print("Cur hPa:"); 


  buttonState = digitalRead(buttonPin);
  float pressure_hPa = mpr.readPressure();
  Serial.print("Pressure (hPa): "); Serial.println(String(pressure_hPa));
  float pressureBar = pressure_hPa / 1000;
  Serial.print("Pressure (Bar): "); Serial.println(String(pressureBar));
  Serial.print("Light is : "); Serial.println(state);
  Serial.print("lowPoint : "); Serial.print(String(lowPoint)); Serial.println(" bar (Absolut) REGISTRED");
  Serial.print("triggerPressure : "); Serial.print(String(triggerPressure)); Serial.println(" bar (Absolut) REGISTRED");
  Serial.println();
  lcd.setCursor(9, 0);
  lcd.print(String(pressureBar));
  lcd.setCursor(9, 1);
  lcd.print(String(pressure_hPa));
  if (buttonState == HIGH) {    // Normally must be true everytime
    if (pressureBar >= triggerPressure) {
      // Turn on the LED to indicate we're going to flip on the vacuum
      digitalWrite(ledPin, HIGH);
      digitalWrite(relayPin, HIGH);
      state = "on";
    } else if (pressureBar <= lowPoint) {
      // Turn off the LED and relay
      digitalWrite(ledPin, LOW);
      digitalWrite(relayPin, LOW);
      state = "off";
    } /*else {
      digitalWrite(ledPin, LOW);
      digitalWrite(relayPin, LOW);
      state = "off";
    }*/
  } else if (buttonState == HIGH) {
    digitalWrite(ledPin, LOW);
    digitalWrite(relayPin, LOW);
    state = "off";
  } else {
    digitalWrite(ledPin, HIGH);
    digitalWrite(relayPin, HIGH);
    state = "on";
  }
  delay(1000);
  }


}

// code stored in the sketch: vacbedControl_Gotcha.ino
#include <Arduino.h>


/*!
 * @file mprls_simpletest.ino
 *
 * A basic test of the sensor with default settings
 * 
 * Designed specifically to work with the MPRLS sensor from Adafruit
 * ----> https://www.adafruit.com/products/3965
 *
 * These sensors use I2C to communicate, 2 pins (SCL+SDA) are required
 * to interface with the breakout.
 *
 * Adafruit invests time and resources providing this open source code,
 * please support Adafruit and open-source hardware by purchasing
 * products from Adafruit!
 *
 * Written by Limor Fried/Ladyada for Adafruit Industries.  
 *
 * MIT license, all text here must be included in any redistribution.
 * 
 * Code is based on the above, with added functionality for an override button,
 * and an LED indicator
 * 
 */


 /*
  * 1 Bar = 14.61 PSI
  * -0.25 Bar = (1-0.25) = 0.75 Bar = 10.88 PSI
  * Sources : https://www.gflow.fr/upload/files/psi-bar.pdf and http://dominique.melotti.pagesperso-orange.fr/bar.htm
  * 1 Bar = 1000 Hectopascals
  * 0.75 Bar = 750 hPa
  * Source : https://convertlive.com/fr/u/convert/barres/a/hectopascals#0.75
  * -0.25 Bar = 850 hPa = +0.75 Bar
  */
 
#include <Wire.h>
#include <Adafruit_MPRLS.h>
#include <LiquidCrystal.h>


// You dont *need* a reset and EOC pin for most uses, so we set to -1 and don't connect
#define RESET_PIN  -1  // set to any GPIO pin # to hard-reset on begin()
#define EOC_PIN    -1  // set to any GPIO pin to read end-of-conversion by pin
Adafruit_MPRLS mpr = Adafruit_MPRLS(RESET_PIN, EOC_PIN);


// Pin Settings
const int ledPin =  22;
const int buttonPin = 13;
const int relayPin = 26;
const int contrastPin = 6;
const int potentiometerPin = A15;
const int buttonFPin = 7;


// SET THE PRESSURE HERE (In absolute Bar)
float triggerPressure = 1.01;  // In ABS - Default is 0.825 (-0.175 bar)
float lowPoint = 0.85;         // In ABS - Default is 0.750 (-0.250 bar)


// BUTTOM
// The button take effect between the lowPoint and the triggerPressur for restart the vacuum until the the lowPoint.
int buttonState = 0;
int buttonFState = 0;
String state;
float potentiometerValue;


// Settings for the LCD:
const int rs = 12, en = 11, d4 = 5, d5 = 4, d6 = 3, d7 = 2;
LiquidCrystal lcd(rs, en, d4, d5, d6, d7);
int Contrast=75;


// Settings for initialisation
int EOI = 0;
int Stop;



void setup() {
  Serial.begin(115200);
  analogWrite(contrastPin,Contrast);
  Serial.println("MPRLS Simple Test");
  lcd.begin(16, 2);
  if (! mpr.begin()) {
    Serial.println("Failed to communicate with MPRLS sensor, check wiring?");
    while (1) {
      delay(10);
    }
  }
  Serial.println("Found MPRLS sensor");


  // initialize the LED pin as an output:
  pinMode(ledPin, OUTPUT);
  pinMode(relayPin, OUTPUT);
  pinMode(buttonPin, INPUT_PULLUP);
  pinMode(buttonFPin, INPUT_PULLUP); // Bouton est passant en PULLUP


  // Forced work (only at the startup or after RESET)
  buttonFState = digitalRead(buttonFPin);
  Serial.print("Etat du bouton de marche forcée : "); Serial.println(buttonFState);
  if (buttonFState == 0) { // Infinite loop
    Serial.println();
    Serial.println("*****************");
    Serial.println("**** WARNING ****");
    Serial.println("*****************");
    Serial.println();
    while (1) {
      float pressure_hPa = mpr.readPressure();
      digitalWrite(ledPin, HIGH);
      digitalWrite(relayPin, HIGH);
      state = "on";
      Serial.print("Pressure (hPa): "); Serial.println(String(pressure_hPa));
      Serial.println("FORCED WORK ! BE CAREFULL !!!");
      lcd.clear();
      lcd.print(" NO LIMITS !!!! ");
      lcd.setCursor(0, 1);
      lcd.print("RESET TO STOP IT");
      delay (1000);
    }
  }



  // INITIALISATION
  lcd.clear();
  lcd.print(" INITIALISATION");
  lcd.setCursor(0, 1);
  lcd.print("****************");
  Serial.print("buttonState : "); Serial.println(String(buttonState));
  Serial.print("potentiometerValue : "); Serial.println(analogRead(A15));
  Serial.println();
  delay(2000);


}



void loop() {



// Adjust the trigger and low points
while (EOI != 2) { // Condition à vérifier pour rester dans la boucle jusqu'à ce que...
  if (EOI == 0) {
    // Setting the Low point
    buttonState = digitalRead(buttonPin);
    lcd.clear();
    lcd.print("SET low point :");
    lcd.setCursor(0, 1);
    potentiometerValue = (analogRead(potentiometerPin) * (-0.33/1024));
    lcd.print(potentiometerValue); lcd.print(" bar");


    // Condition de sortie du WHILE
    if (buttonState == LOW) {
      EOI = 1;
      lowPoint = 1 + potentiometerValue;
    }
    Serial.print("buttonState : "); Serial.println(String(buttonState)); 
    Serial.print("EOI : "); Serial.println(String(EOI));
    Serial.print("lowPoint : "); Serial.print(String(lowPoint)); Serial.println(" bar (Absolut) by DEFAULT");
    Serial.println();
    delay(400); 
  } else {
    if (EOI == 1) {
      // Settings the Trigger point
      buttonState = digitalRead(buttonPin);
      lcd.clear();
      lcd.print("SET trigger pt :");
      lcd.setCursor(0, 1);
      potentiometerValue = (analogRead(potentiometerPin) * (-0.23/1024));
      lcd.print(potentiometerValue); lcd.print(" bar");
      
      // Condition de sortie du WHILE
      if (buttonState == LOW) {
        EOI = 2;
        triggerPressure = 1 + potentiometerValue;
      }
      Serial.print("buttonState : "); Serial.println(String(buttonState)); 
      Serial.print("EOI : "); Serial.println(String(EOI));
      Serial.print("lowPoint : "); Serial.print(String(lowPoint)); Serial.println(" bar (Absolut) REGISTRED");
      Serial.print("triggerPressure : "); Serial.print(String(triggerPressure)); Serial.println(" bar (Absolut) by DEFAULT");
      Serial.println();
      delay(400);
    }
  }
}



/*
*  We're going to need to read the pressure, and then decide if we need to trigger the relay for the vacuum
*  once we trigger the vacuum, we want to check the pressure every second until it hits the expected pressure,
*  once it goes above the preferred pressure, it will close the relay again.
*
*  Beetwen the lowPoint and the triggerPressure, the vaccum system can be restarted if the "OK - RESTART" button is pressed. 
*/


lcd.clear();
lcd.print("LET'S STARTED !!");
delay(2500);
lcd.clear();


while (1) { // Infinite loop
  lcd.print("Cur Bar:");
  lcd.setCursor(0, 1);
  lcd.print("Cur hPa:"); 


  buttonState = digitalRead(buttonPin);
  float pressure_hPa = mpr.readPressure();
  Serial.print("Pressure (hPa): "); Serial.println(String(pressure_hPa));
  float pressureBar = pressure_hPa / 1000;
  Serial.print("Pressure (Bar): "); Serial.println(String(pressureBar));
  Serial.print("Light is : "); Serial.println(state);
  Serial.print("lowPoint : "); Serial.print(String(lowPoint)); Serial.println(" bar (Absolut) REGISTRED");
  Serial.print("triggerPressure : "); Serial.print(String(triggerPressure)); Serial.println(" bar (Absolut) REGISTRED");
  Serial.println();
  lcd.setCursor(9, 0);
  lcd.print(String(pressureBar));
  lcd.setCursor(9, 1);
  lcd.print(String(pressure_hPa));
  if (buttonState == HIGH) {    // Normally must be true everytime
    if (pressureBar >= triggerPressure) {
      // Turn on the LED to indicate we're going to flip on the vacuum
      digitalWrite(ledPin, HIGH);
      digitalWrite(relayPin, HIGH);
      state = "on";
    } else if (pressureBar <= lowPoint) {
      // Turn off the LED and relay
      digitalWrite(ledPin, LOW);
      digitalWrite(relayPin, LOW);
      state = "off";
    } /*else {
      digitalWrite(ledPin, LOW);
      digitalWrite(relayPin, LOW);
      state = "off";
    }*/
  } else if (buttonState == HIGH) {
    digitalWrite(ledPin, LOW);
    digitalWrite(relayPin, LOW);
    state = "off";
  } else {
    digitalWrite(ledPin, HIGH);
    digitalWrite(relayPin, HIGH);
    state = "on";
  }
  delay(1000);
  }


}
