# Fritzing sketch v03.00.00 (saved by Fritzing 0.9.10b)
breadboards: 2

parts:
  Composant1 = Arduino Mega 2560 (Rev3)
  Composant2 = Adafruit MPRLS Sensor Breakout [part_number=3965]
  U1 = POT [knob_status=50% power=0.5W package=pot_mammoth]
  U2 = POT [knob_status=50% power=0.5W package=pot_mammoth]
  R1 = Resistor [tolerance=±5% resistance=330 package="0402 [SMD]"]
  S1 = Pushbutton [package="[THT]"]
  S2 = Pushbutton [package="[THT]"]
  S3 = Pushbutton [package="[THT]"]
  LED2 = smd LED [color="Red (633nm)" package="1206 [SMD]"]
  LCD1 = LCD screen
  R2 = Resistor [tolerance=±5% resistance=220 package="0402 [SMD]"]
  LED3 = RGB LED (com. anode, rbg) [package="5 mm [THT]"]
  R3 = Resistor [tolerance=±5% resistance=330 package="0402 [SMD]"]
  R4 = Resistor [tolerance=±5% resistance=330 package="0402 [SMD]"]

nets:
  N1: Composant1.A14, U2.A
  N2: Composant1.A15, U1.A
  N3: Composant1.A0, R4.Pin_0
  N4: Composant1.A1, R3.Pin_0
  N5: Composant1.A2, R1.Pin_0
  N6: Composant1.D21/SCL, Composant2.SCL
  N7: Composant1.D20/SDA, Composant2.SDA
  N8: Composant1.D18/TX1, S2.Pin_3, S2.Pin_4
  GND: Composant1.GND, Composant2.GND, U1.E, U2.E, S1.Pin_1, S1.Pin_2, S2.Pin_1, S2.Pin_2, S3.Pin_1, S3.Pin_2, LED2.cathode, LCD1.VSS, LCD1.R/W, LCD1.LED-, LED3.blue_cathode
  N9: Composant1.D12_PWM, LCD1.RS
  N10: Composant1.D11_PWM, LCD1.E
  N11: Composant1.RESET, S3.Pin_3, S3.Pin_4
  3V3: Composant1.3V3, Composant2.3.3V
  N12: Composant1.D2_PWM, LCD1.DB7
  N13: Composant1.D3_PWM, LCD1.DB6
  N14: Composant1.D4_PWM, LCD1.DB5
  N15: Composant1.D5_PWM, LCD1.DB4
  N16: Composant1.D6_PWM, LCD1.V0
  N17: Composant1.D22, R2.Pin_1
  N18: Composant1.D26, S1.Pin_3, S1.Pin_4
  N19: U1.S, U2.S, LCD1.VDD, LCD1.LED+
  N20: R1.Pin_1, LED3.red_cathode
  N21: LED2.anode, R2.Pin_0
  N22: LED3.common_anode, R3.Pin_1
  N23: LED3.green_cathode, R4.Pin_1

notes:
  NO LIMITS
  VALIDATION
  RESET
  Action
  Pt. bas (low)
  Pt. haut (max)
  Led de service

custom parts:
  Adafruit MPRLS Sensor Breakout: This pressure sensor is special because it comes with a metal port - you can easily attach a tube to it, to measure air pressure inside a close space. In particular we think this would be a great sensor for use with making DIY assistive tech "Sip & Puff" interfaces, or measuring the pressure within a vacuum chamber or other pressurized container. The port is made of stainless steel and is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

// code stored in the sketch: Untitled2.ino
// ToDo list
// Led RGB pour les états du dispositif
// Boucler le test du capteur (COM ok vs NOK)
// Précision sur la dixaine uniquement pour les potentiomètres
// Inverser le sens d'encodage des potentiomètres
// Ajouter un symbale en tête de ligne #2 dans loop pour indiquer ce que doit faire la pression (up/down)



#include <Arduino.h>
#include <Wire.h>
#include <Adafruit_MPRLS.h>
#include <LiquidCrystal.h>



// You dont *need* a reset and EOC pin for most uses, so we set to -1 and don't connect
#define RESET_PIN  -1  // set to any GPIO pin # to hard-reset on begin()
#define EOC_PIN    -1  // set to any GPIO pin to read end-of-conversion by pin
Adafruit_MPRLS mpr = Adafruit_MPRLS(RESET_PIN, EOC_PIN);



// Definition des Pin;
const byte LedAction =  22;
const byte RelayMoteur = 24;
const byte ButtonValidation = 26;
const byte ButtonForcer = 18;
const int PinPotentioH = A15;
const int PinPotentioL = A14;
const byte LedTest = 38;


// Configuration des seuils Bas / Haut;
// Les pression sont données en BAR (bar) donc une pression relative par rapport à la pression ambiante.
// Cette pression ambiante est exprimée en Hecto Pascal (hPa) est vaut 1010 hPa environ.
// La convertion est donc environ de 1000 et donne 1 bar à une pression ambiante.
// Une dépression (exprimée en bar) est évaluée par rapport à la pression ambiante et est donc négative.
// Une dépression (exprimée en hPa) est évaluée par rapport à la pression ambiante et est donc toujours positive.
volatile int lowPoint;  // Point le plus  bas (low) sur l'echelle de la dépression. -0.3 bar = 700 hPa
volatile int maxPoint;  // Point le plus haut (max) sur l'echelle de la dépression. -0.2 bar = 800 hPa


String pressure_hpa;


float ValuePotentioH;
float ValuePotentioL;


// Parametre LCD ;
const int rs = 12, en = 11, d4 = 5, d5 = 4, d6 = 3, d7 = 2;
LiquidCrystal lcd(rs, en, d4, d5, d6, d7);
const int contrastPin = 6;
int Contrast=75;    // Contraste de 0 à 100



// Settings for initialisation
int debugMode = 1;


// Fonction d'interruption
void Forced() {
  maxPoint = 0;
  lowPoint = 0;
  Serial.println("Je suis là !");
}


// Fonction de boucle infinie en cas de soucis
void functionExit () {
  while (1) {
    digitalWrite(LedTest, LOW);
    delay(100);
    }
}



void setup() {


  // Affectations
  digitalWrite(LedTest, HIGH);
  Serial.begin(115200);
  analogWrite(contrastPin,Contrast);
  pinMode(LedTest, OUTPUT);
  pinMode(LedAction, OUTPUT);
  pinMode(RelayMoteur, OUTPUT);
  pinMode(ButtonValidation, INPUT_PULLUP);
  pinMode(ButtonForcer, INPUT_PULLUP); // Bouton est passant en PULLUP


  // Interruption
  attachInterrupt(digitalPinToInterrupt(ButtonForcer), Forced, FALLING); // Déclenchement quand une chute vers l'état BAS.


  // Check the MPRLS sensor
  Serial.println("MPRLS Simple Test");
  lcd.begin(16, 2);
  lcd.print("Hello");


  if (! mpr.begin(0x18)) { // Adresse par défaut 0x18 pour ce capteur
      Serial.println("Failed to communicate with MPRLS sensor, check wiring?");
      lcd.clear();
       lcd.setCursor(0, 1);
       lcd.print("Error Com MPRLS");
      functionExit();
  }
  
  Serial.println("Found MPRLS sensor");
  lcd.setCursor(0, 1);
  lcd.print("Setup OK");
  delay(500);


  // Lecture de la pression depus le capteur
  pressure_hpa = mpr.readPressure();
  
  // INITIALISATION
  lcd.clear();
  lcd.print(" INITIALISATION");
   lcd.setCursor(0, 1);
   lcd.print("****************");
  delay(2000);


  do {
    lcd.clear();
    lcd.print("SET low. point :");
     lcd.setCursor(0, 1);
     lowPoint = ((int)analogRead(PinPotentioL));
     lcd.print(lowPoint);
     lcd.print(" hPa");
    delay(100);
    if (debugMode > 0) {
      Serial.print("Valeure prise par lowPoint : ");
      Serial.println(lowPoint);
       Serial.print("Etat du bouton de validation : ");
       Serial.println(String(digitalRead(ButtonValidation)));
    }
  }
  while (digitalRead(ButtonValidation) == HIGH);
  delay(350); // Evite de passer la séquence si le bouton n'est pas relaché assez vite.
  
  do {
    lcd.clear();
    lcd.print("SET max. point :");
     lcd.setCursor(0, 1);
     maxPoint = ((int)analogRead(PinPotentioH));
     lcd.print(maxPoint);
     lcd.print(" hPa");
    delay(100);
    if (debugMode > 0) {
      Serial.print("Valeure prise par maxPoint : ");
      Serial.println(lowPoint);
       Serial.print("Etat du bouton de validation : ");
       Serial.println(String(digitalRead(ButtonValidation)));
    }
  }
  while(digitalRead(ButtonValidation) == HIGH);


}


void loop() {


  // Affichage de la datas
  if (debugMode > 0) {
  Serial.print("Pression actuelle : ");
  Serial.print(pressure_hpa);
  Serial.println(" hPa");
  
  ValuePotentioH = (analogRead(PinPotentioH));
  Serial.print("Valeure prise par PotentioH :");
  Serial.println(ValuePotentioH);
  
  ValuePotentioL = (analogRead(PinPotentioL));
  Serial.print("Valeure prise par PotentioL :");
  Serial.println(ValuePotentioL);


  Serial.print("Etat du bouton de validation : ");
  Serial.println(String(digitalRead(ButtonValidation)));
  }


  lcd.clear();
   lcd.print("LET'S STARTED !!");
  delay(2000);
  lcd.clear();


  while (1) { // Boucle infinie
    int pressure_hpa = mpr.readPressure();
    lcd.setCursor(0, 0);
    lcd.print("hPa Actual: ");
    lcd.print(pressure_hpa);
    lcd.print(" "); // Efface le reste de la ligne


    if (pressure_hpa >= maxPoint) { // En fonction
      digitalWrite(LedAction, HIGH);
      digitalWrite(RelayMoteur, HIGH);
      lcd.setCursor(5, 1);
      lcd.print("Next : ");
      lcd.print(lowPoint);
      lcd.print("   ");
      delay(300);
    }
    else if (pressure_hpa <= lowPoint) { // En attente
      digitalWrite(LedAction, LOW);
      digitalWrite(RelayMoteur, LOW);
      lcd.setCursor(5, 1);
      lcd.print("Next : ");
      lcd.print(maxPoint);
      lcd.print("   ");
      delay(300);
    }
  }
}

// code stored in the sketch: v03.00.00.ino
#include <Arduino.h>
#include <Wire.h>
#include <Adafruit_MPRLS.h>
#include <LiquidCrystal.h>



// You dont *need* a reset and EOC pin for most uses, so we set to -1 and don't connect
#define RESET_PIN  -1  // set to any GPIO pin # to hard-reset on begin()
#define EOC_PIN    -1  // set to any GPIO pin to read end-of-conversion by pin
Adafruit_MPRLS mpr = Adafruit_MPRLS(RESET_PIN, EOC_PIN);



// Attribution des Pin;
static const byte LedAction =  22;
static const byte RelayMoteur = 24;
static const byte ButtonValidation = 26;
static const byte ButtonForcer = 18;
static const uint8_t PinPotentioH = A15;
static const uint8_t PinPotentioL = A14;


#define LedRGB_R A0
#define LedRGB_G A1
#define LedRGB_B A2


// Configuration des seuils Bas / Haut;
// Les pressions sont données en BAR (bar) donc une pression relative par rapport à la pression ambiante.
// Cette pression ambiante est exprimée en Hecto Pascal (hPa) est vaut 1010 hPa environ.
// La convertion est donc environ de 1000 et donne 1 bar à une pression ambiante.
// Une dépression (exprimée en bar) est évaluée par rapport à la pression ambiante et est donc négative.
// Une dépression (exprimée en hPa) est évaluée par rapport à la pression ambiante et est donc toujours positive.
volatile int lowPoint;  // Point le plus  bas (low) sur l'echelle de la dépression. -0.3 bar = 700 hPa
volatile int maxPoint;  // Point le plus haut (max) sur l'echelle de la dépression. -0.2 bar = 800 hPa


String pressure_hpa;
float ValuePotentioH;
float ValuePotentioL;


// Parametre LCD ;
const int rs = 12, en = 11, d4 = 5, d5 = 4, d6 = 3, d7 = 2;
LiquidCrystal lcd(rs, en, d4, d5, d6, d7);
const int contrastPin = 6;
int Contrast=75;    // Contraste de 0 à 100



// Settings for initialisation
int debugMode = 1;


// Couleur jaune
// setLedRGB(255, 255, 0);
// Couleur orange
// setLedRGB(255, 128, 0);
// Couleur rouge
// setLedRGB(255, 0, 0);
void setLedRGB (int R, int G, int B) {
  analogWrite(LedRGB_R, R);
  analogWrite(LedRGB_G, G);
  analogWrite(LedRGB_B, B);
}


// Fonction d'interruption
void Forced() {
  maxPoint = 0;
  lowPoint = 0;
  Serial.println("Je suis là !");
}


// Fonction de boucle infinie en cas de soucis
void functionExit () {
  while (1) {
    setLedRGB(255, 0, 0);
    delay(100);
    }
}



void setup() {


  // Affectations
  Serial.begin(115200);
  analogWrite(contrastPin,Contrast);


  pinMode(LedRGB_R, OUTPUT);
  pinMode(LedRGB_G, OUTPUT);
  pinMode(LedRGB_B, OUTPUT);


  setLedRGB(0, 0, 255);


  pinMode(LedAction, OUTPUT);
  pinMode(RelayMoteur, OUTPUT);
  pinMode(ButtonValidation, INPUT_PULLUP);
  pinMode(ButtonForcer, INPUT_PULLUP); // Bouton est passant en PULLUP


  // Interruption
  attachInterrupt(digitalPinToInterrupt(ButtonForcer), Forced, FALLING); // Déclenchement quand une chute vers l'état BAS.


  // Check the MPRLS sensor
  Serial.println("MPRLS Simple Test");
  lcd.begin(16, 2);
  lcd.print("Hello");


  if (! mpr.begin(0x18)) { // Adresse par défaut 0x18 pour ce capteur
      Serial.println("Failed to communicate with MPRLS sensor, check wiring?");
      lcd.clear();
       lcd.setCursor(0, 1);
       lcd.print("Error Com MPRLS");
      functionExit();
  }
  
  Serial.println("Found MPRLS sensor");
  lcd.setCursor(0, 1);
  lcd.print("Setup OK");
  delay(500);


  // Lecture de la pression depus le capteur
  pressure_hpa = mpr.readPressure();
  
  // INITIALISATION
  setLedRGB (255, 255, 0);
  lcd.clear();
  lcd.print(" INITIALISATION");
   lcd.setCursor(0, 1);
   lcd.print("****************");
  delay(2000);


  do {
    lcd.clear();
    lcd.print("SET low. point :");
     lcd.setCursor(0, 1);
     lowPoint = ((int)analogRead(PinPotentioL));
     lcd.print(lowPoint);
     lcd.print(" hPa");
    delay(100);
    if (debugMode > 0) {
      Serial.print("Valeure prise par lowPoint : ");
      Serial.println(lowPoint);
       Serial.print("Etat du bouton de validation : ");
       Serial.println(String(digitalRead(ButtonValidation)));
    }
  }
  while (digitalRead(ButtonValidation) == HIGH);
  delay(350); // Evite de passer la séquence si le bouton n'est pas relaché assez vite.
  
  do {
    lcd.clear();
    lcd.print("SET max. point :");
     lcd.setCursor(0, 1);
     maxPoint = ((int)analogRead(PinPotentioH));
     lcd.print(maxPoint);
     lcd.print(" hPa");
    delay(100);
    if (debugMode > 0) {
      Serial.print("Valeure prise par maxPoint : ");
      Serial.println(lowPoint);
       Serial.print("Etat du bouton de validation : ");
       Serial.println(String(digitalRead(ButtonValidation)));
    }
  }
  while(digitalRead(ButtonValidation) == HIGH);


}


void loop() {


  setLedRGB (0, 255, 0);


  // Affichage de la datas
  if (debugMode > 0) {
  Serial.print("Pression actuelle : ");
  Serial.print(pressure_hpa);
  Serial.println(" hPa");
  
  ValuePotentioH = (analogRead(PinPotentioH));
  Serial.print("Valeure prise par PotentioH :");
  Serial.println(ValuePotentioH);
  
  ValuePotentioL = (analogRead(PinPotentioL));
  Serial.print("Valeure prise par PotentioL :");
  Serial.println(ValuePotentioL);


  Serial.print("Etat du bouton de validation : ");
  Serial.println(String(digitalRead(ButtonValidation)));
  }


  lcd.clear();
   lcd.print("LET'S STARTED !!");
  delay(2000);
  lcd.clear();


  while (1) { // Boucle infinie
    int pressure_hpa = mpr.readPressure();
    lcd.setCursor(0, 0);
    lcd.print("hPa Actual: ");
    lcd.print(pressure_hpa);
    lcd.print(" "); // Efface le reste de la ligne


    if (pressure_hpa >= maxPoint) { // En fonction
      digitalWrite(LedAction, HIGH);
      digitalWrite(RelayMoteur, HIGH);
      lcd.setCursor(5, 1);
      lcd.print("Next : ");
      lcd.print(lowPoint);
      lcd.print("   ");
      delay(300);
    }
    else if (pressure_hpa <= lowPoint) { // En attente
      digitalWrite(LedAction, LOW);
      digitalWrite(RelayMoteur, LOW);
      lcd.setCursor(5, 1);
      lcd.print("Next : ");
      lcd.print(maxPoint);
      lcd.print("   ");
      delay(300);
    }
  }
}

// code stored in the sketch: v2.0.ino
#include <Arduino.h>
#include <Wire.h>
#include <Adafruit_MPRLS.h>
#include <LiquidCrystal.h>


// You dont *need* a reset and EOC pin for most uses, so we set to -1 and don't connect
#define RESET_PIN  -1  // set to any GPIO pin # to hard-reset on begin()
#define EOC_PIN    -1  // set to any GPIO pin to read end-of-conversion by pin
Adafruit_MPRLS mpr = Adafruit_MPRLS(RESET_PIN, EOC_PIN);


// Definition des Pin;
const byte LedAction =  22;
const byte RelayMoteur = 24;
const byte ButtonValidation = 26;
const byte ButtonForcer = 18;
const int PinPotentioH = A15;
const int PinPotentioL = A14;
const byte LedTest = 38;

// Configuration des seuils Bas / Haut;
// Les pression sont données en BAR (bar) donc une pression relative par rapport à la pression ambiante.
// Cette pression ambiante est exprimée en Hecto Pascal (hPa) est vaut 1010 hPa environ.
// La convertion est donc environ de 1000 et donne 1 bar à une pression ambiante.
// Une dépression (exprimée en bar) est évaluée par rapport à la pression ambiante et est donc négative.
// Une dépression (exprimée en hPa) est évaluée par rapport à la pression ambiante et est donc toujours positive.
volatile int lowPoint;  // Point le plus  bas (low) sur l'echelle de la dépression. -0.3 bar = 700 hPa
volatile int maxPoint;  // Point le plus haut (max) sur l'echelle de la dépression. -0.2 bar = 800 hPa

String pressure_hpa;

float ValuePotentioH;
float ValuePotentioL;

// Parametre LCD ;
const int rs = 12, en = 11, d4 = 5, d5 = 4, d6 = 3, d7 = 2;
LiquidCrystal lcd(rs, en, d4, d5, d6, d7);
const int contrastPin = 6;
int Contrast=75;    // Contraste de 0 à 100


// Settings for initialisation
int debugMode = 1;

void Forced() {
  maxPoint = 0;
  lowPoint = 0;
  Serial.println("Je suis là !");
  lcd.clear();
}


void setup() {
  
  // Interruption
  attachInterrupt(digitalPinToInterrupt(ButtonForcer), Forced, FALLING); // Déclenchement quand une chute vers l'état BAS.

  Serial.begin(115200);
  analogWrite(contrastPin,Contrast);
  pinMode(LedTest, OUTPUT);
  pinMode(LedAction, OUTPUT);
  pinMode(RelayMoteur, OUTPUT);
  pinMode(ButtonValidation, INPUT_PULLUP);
  pinMode(ButtonForcer, INPUT_PULLUP); // Bouton est passant en PULLUP

  // Check the MPRLS sensor
  Serial.println("MPRLS Simple Test");
  lcd.begin(16, 2);
  lcd.print("Hello");

  if (! mpr.begin(0x18)) { // Adresse par défaut 0x18 pour ce capteur
      Serial.println("Failed to communicate with MPRLS sensor, check wiring?");
      lcd.setCursor(0, 1);
      lcd.print("Error Com MPRLS");
      // fonctionExit();
  }
  
  Serial.println("Found MPRLS sensor");
  lcd.setCursor(0, 1);
   lcd.print("Setup OK");
  delay(500);

  // Lecture de la pression depus le capteur
  pressure_hpa = mpr.readPressure();
  
  // INITIALISATION
  lcd.clear();
  lcd.print(" INITIALISATION");
  lcd.setCursor(0, 1);
  lcd.print("****************");
  delay(2000);

  do {
    lcd.clear();
    lcd.print("SET low. point :");
    lcd.setCursor(0, 1);
    lowPoint = ((int)analogRead(PinPotentioL));
    lcd.print(lowPoint);
     lcd.print(" hPa");
    delay(100);
    if (debugMode > 0) {
      Serial.print("Valeure prise par lowPoint : ");
        Serial.println(lowPoint);
      Serial.print("Etat du bouton de validation : ");
      Serial.println(String(digitalRead(ButtonValidation)));
    }
  }
  while (digitalRead(ButtonValidation) == HIGH);
  delay(350); // Evite de passer la séquence si le bouton n'est pas relaché assez vite.
  
  do {
    lcd.clear();
    lcd.print("SET max. point :");
    lcd.setCursor(0, 1);
    maxPoint = ((int)analogRead(PinPotentioH));
    lcd.print(maxPoint);
     lcd.print(" hPa");
    delay(100);
    if (debugMode > 0) {
      Serial.print("Valeure prise par maxPoint : ");
        Serial.println(lowPoint);
      Serial.print("Etat du bouton de validation : ");
      Serial.println(String(digitalRead(ButtonValidation)));
    }
  }
  while(digitalRead(ButtonValidation) == HIGH);

}

void loop() {

  // Affichage de la datas
  if (debugMode > 0) {
  Serial.print("Pression actuelle : ");
   Serial.print(pressure_hpa);
    Serial.println(" hPa");
  
  ValuePotentioH = (analogRead(PinPotentioH));
  Serial.print("Valeure prise par PotentioH :");
   Serial.println(ValuePotentioH);
  
  ValuePotentioL = (analogRead(PinPotentioL));
  Serial.print("Valeure prise par PotentioL :");
   Serial.println(ValuePotentioL);
  
  digitalWrite(LedTest, HIGH);

  Serial.print("Etat du bouton de validation : ");
   Serial.println(String(digitalRead(ButtonValidation)));
  }

  lcd.clear();
   lcd.print("LET'S STARTED !!");
  delay(2000);
  lcd.clear();

  while (1) { // Boucle infinie
    int pressure_hpa = mpr.readPressure();
    lcd.setCursor(0, 0);
     lcd.print("hPa Actual: ");
      lcd.print(pressure_hpa);
       lcd.print(" ");

    if (pressure_hpa >= maxPoint) { // Turn on the LED to indicate we're going to flip on the vacuum
      digitalWrite(LedAction, HIGH);
      digitalWrite(RelayMoteur, HIGH);
      lcd.setCursor(5, 1);
      lcd.print("Next : ");
       lcd.print(lowPoint);
      delay(300);
    }
    else if (pressure_hpa <= lowPoint) { // Turn off the LED and relay
      digitalWrite(LedAction, LOW);
      digitalWrite(RelayMoteur, LOW);
      lcd.setCursor(5, 1);
      lcd.print("Next : ");
       lcd.print(maxPoint);
      delay(300);
    }
  }
}

// code stored in the sketch: v2.1.ino
// ToDo list
// Led RGB pour les états du dispositif
// Boucler le test du capteur (COM ok vs NOK)
// Précision sur la dixaine uniquement pour les potentiomètres
// Inverser le sens d'encodage des potentiomètres
// Ajouter un symbale en tête de ligne #2 dans loop pour indiquer ce que doit faire la pression (up/down)



#include <Arduino.h>
#include <Wire.h>
#include <Adafruit_MPRLS.h>
#include <LiquidCrystal.h>



// You dont *need* a reset and EOC pin for most uses, so we set to -1 and don't connect
#define RESET_PIN  -1  // set to any GPIO pin # to hard-reset on begin()
#define EOC_PIN    -1  // set to any GPIO pin to read end-of-conversion by pin
Adafruit_MPRLS mpr = Adafruit_MPRLS(RESET_PIN, EOC_PIN);



// Definition des Pin;
const byte LedAction =  22;
const byte RelayMoteur = 24;
const byte ButtonValidation = 26;
const byte ButtonForcer = 18;
const int PinPotentioH = A15;
const int PinPotentioL = A14;
const byte LedTest = 38;


// Configuration des seuils Bas / Haut;
// Les pression sont données en BAR (bar) donc une pression relative par rapport à la pression ambiante.
// Cette pression ambiante est exprimée en Hecto Pascal (hPa) est vaut 1010 hPa environ.
// La convertion est donc environ de 1000 et donne 1 bar à une pression ambiante.
// Une dépression (exprimée en bar) est évaluée par rapport à la pression ambiante et est donc négative.
// Une dépression (exprimée en hPa) est évaluée par rapport à la pression ambiante et est donc toujours positive.
volatile int lowPoint;  // Point le plus  bas (low) sur l'echelle de la dépression. -0.3 bar = 700 hPa
volatile int maxPoint;  // Point le plus haut (max) sur l'echelle de la dépression. -0.2 bar = 800 hPa


String pressure_hpa;


float ValuePotentioH;
float ValuePotentioL;


// Parametre LCD ;
const int rs = 12, en = 11, d4 = 5, d5 = 4, d6 = 3, d7 = 2;
LiquidCrystal lcd(rs, en, d4, d5, d6, d7);
const int contrastPin = 6;
int Contrast=75;    // Contraste de 0 à 100



// Settings for initialisation
int debugMode = 1;


// Fonction d'interruption
void Forced() {
  maxPoint = 0;
  lowPoint = 0;
  Serial.println("Je suis là !");
}


// Fonction de boucle infinie en cas de soucis
void functionExit () {
  while (1) {
    digitalWrite(LedTest, LOW);
    delay(100);
    }
}



void setup() {


  // Affectations
  digitalWrite(LedTest, HIGH);
  Serial.begin(115200);
  analogWrite(contrastPin,Contrast);
  pinMode(LedTest, OUTPUT);
  pinMode(LedAction, OUTPUT);
  pinMode(RelayMoteur, OUTPUT);
  pinMode(ButtonValidation, INPUT_PULLUP);
  pinMode(ButtonForcer, INPUT_PULLUP); // Bouton est passant en PULLUP


  // Interruption
  attachInterrupt(digitalPinToInterrupt(ButtonForcer), Forced, FALLING); // Déclenchement quand une chute vers l'état BAS.


  // Check the MPRLS sensor
  Serial.println("MPRLS Simple Test");
  lcd.begin(16, 2);
  lcd.print("Hello");


  if (! mpr.begin(0x18)) { // Adresse par défaut 0x18 pour ce capteur
      Serial.println("Failed to communicate with MPRLS sensor, check wiring?");
      lcd.clear();
       lcd.setCursor(0, 1);
       lcd.print("Error Com MPRLS");
      functionExit();
  }
  
  Serial.println("Found MPRLS sensor");
  lcd.setCursor(0, 1);
  lcd.print("Setup OK");
  delay(500);


  // Lecture de la pression depus le capteur
  pressure_hpa = mpr.readPressure();
  
  // INITIALISATION
  lcd.clear();
  lcd.print(" INITIALISATION");
   lcd.setCursor(0, 1);
   lcd.print("****************");
  delay(2000);


  do {
    lcd.clear();
    lcd.print("SET low. point :");
     lcd.setCursor(0, 1);
     lowPoint = ((int)analogRead(PinPotentioL));
     lcd.print(lowPoint);
     lcd.print(" hPa");
    delay(100);
    if (debugMode > 0) {
      Serial.print("Valeure prise par lowPoint : ");
      Serial.println(lowPoint);
       Serial.print("Etat du bouton de validation : ");
       Serial.println(String(digitalRead(ButtonValidation)));
    }
  }
  while (digitalRead(ButtonValidation) == HIGH);
  delay(350); // Evite de passer la séquence si le bouton n'est pas relaché assez vite.
  
  do {
    lcd.clear();
    lcd.print("SET max. point :");
     lcd.setCursor(0, 1);
     maxPoint = ((int)analogRead(PinPotentioH));
     lcd.print(maxPoint);
     lcd.print(" hPa");
    delay(100);
    if (debugMode > 0) {
      Serial.print("Valeure prise par maxPoint : ");
      Serial.println(lowPoint);
       Serial.print("Etat du bouton de validation : ");
       Serial.println(String(digitalRead(ButtonValidation)));
    }
  }
  while(digitalRead(ButtonValidation) == HIGH);


}


void loop() {


  // Affichage de la datas
  if (debugMode > 0) {
  Serial.print("Pression actuelle : ");
  Serial.print(pressure_hpa);
  Serial.println(" hPa");
  
  ValuePotentioH = (analogRead(PinPotentioH));
  Serial.print("Valeure prise par PotentioH :");
  Serial.println(ValuePotentioH);
  
  ValuePotentioL = (analogRead(PinPotentioL));
  Serial.print("Valeure prise par PotentioL :");
  Serial.println(ValuePotentioL);


  Serial.print("Etat du bouton de validation : ");
  Serial.println(String(digitalRead(ButtonValidation)));
  }


  lcd.clear();
   lcd.print("LET'S STARTED !!");
  delay(2000);
  lcd.clear();


  while (1) { // Boucle infinie
    int pressure_hpa = mpr.readPressure();
    lcd.setCursor(0, 0);
    lcd.print("hPa Actual: ");
    lcd.print(pressure_hpa);
    lcd.print(" "); // Efface le reste de la ligne


    if (pressure_hpa >= maxPoint) { // En fonction
      digitalWrite(LedAction, HIGH);
      digitalWrite(RelayMoteur, HIGH);
      lcd.setCursor(5, 1);
      lcd.print("Next : ");
      lcd.print(lowPoint);
      lcd.print("   ");
      delay(300);
    }
    else if (pressure_hpa <= lowPoint) { // En attente
      digitalWrite(LedAction, LOW);
      digitalWrite(RelayMoteur, LOW);
      lcd.setCursor(5, 1);
      lcd.print("Next : ");
      lcd.print(maxPoint);
      lcd.print("   ");
      delay(300);
    }
  }
}

// code stored in the sketch: v3.0.ino
// ToDo list
// Boucler le test du capteur (COM ok vs NOK)
// Précision sur la dixaine uniquement pour les potentiomètres
// Inverser le sens d'encodage des potentiomètres
// Ajouter un symbale en tête de ligne #2 dans loop pour indiquer ce que doit faire la pression (up/down)


// Inspiré de : https://gitlab.com/pleasurepi/vacbedcontrol @halon1301 sur Twitter



#include <Arduino.h>
#include <Wire.h>
#include <Adafruit_MPRLS.h>
#include <LiquidCrystal.h>



// You dont *need* a reset and EOC pin for most uses, so we set to -1 and don't connect
#define RESET_PIN  -1  // set to any GPIO pin # to hard-reset on begin()
#define EOC_PIN    -1  // set to any GPIO pin to read end-of-conversion by pin
Adafruit_MPRLS mpr = Adafruit_MPRLS(RESET_PIN, EOC_PIN);



// Attribution des Pin;
static const byte LedAction =  22;
static const byte RelayMoteur = 24;
static const byte ButtonValidation = 26;
static const byte ButtonForcer = 18;
static const uint8_t PinPotentioH = A15;
static const uint8_t PinPotentioL = A14;


#define LedRGB_R A0
#define LedRGB_G A1
#define LedRGB_B A2


// Configuration des seuils Bas / Haut;
// Les pression sont données en BAR (bar) donc une pression relative par rapport à la pression ambiante.
// Cette pression ambiante est exprimée en Hecto Pascal (hPa) est vaut 1010 hPa environ.
// La convertion est donc environ de 1000 et donne 1 bar à une pression ambiante.
// Une dépression (exprimée en bar) est évaluée par rapport à la pression ambiante et est donc négative.
// Une dépression (exprimée en hPa) est évaluée par rapport à la pression ambiante et est donc toujours positive.
volatile int lowPoint;  // Point le plus  bas (low) sur l'echelle de la dépression. -0.3 bar = 700 hPa
volatile int maxPoint;  // Point le plus haut (max) sur l'echelle de la dépression. -0.2 bar = 800 hPa


String pressure_hpa;
float ValuePotentioH;
float ValuePotentioL;


// Parametre LCD ;
const int rs = 12, en = 11, d4 = 5, d5 = 4, d6 = 3, d7 = 2;
LiquidCrystal lcd(rs, en, d4, d5, d6, d7);
const int contrastPin = 6;
int Contrast=75;    // Contraste de 0 à 100



// Settings for initialisation
int debugMode = 1;


// Couleur jaune
// setLedRGB(255, 255, 0);
// Couleur orange
// setLedRGB(255, 128, 0);
// Couleur rouge
// setLedRGB(255, 0, 0);
void setLedRGB (int R, int G, int B) {
  analogWrite(LedRGB_R, R);
  analogWrite(LedRGB_G, G);
  analogWrite(LedRGB_B, B);
}


// Fonction d'interruption
void Forced() {
  maxPoint = 0;
  lowPoint = 0;
  Serial.println("Je suis là !");
}


// Fonction de boucle infinie en cas de soucis
void functionExit () {
  while (1) {
    setLedRGB(255, 0, 0);
    delay(100);
    }
}



void setup() {


  // Affectations
  Serial.begin(115200);
  analogWrite(contrastPin,Contrast);


  pinMode(LedRGB_R, OUTPUT);
  pinMode(LedRGB_G, OUTPUT);
  pinMode(LedRGB_B, OUTPUT);


  setLedRGB(0, 0, 255);


  pinMode(LedAction, OUTPUT);
  pinMode(RelayMoteur, OUTPUT);
  pinMode(ButtonValidation, INPUT_PULLUP);
  pinMode(ButtonForcer, INPUT_PULLUP); // Bouton est passant en PULLUP


  // Interruption
  attachInterrupt(digitalPinToInterrupt(ButtonForcer), Forced, FALLING); // Déclenchement quand une chute vers l'état BAS.


  // Check the MPRLS sensor
  Serial.println("MPRLS Simple Test");
  lcd.begin(16, 2);
  lcd.print("Hello");


  if (! mpr.begin(0x18)) { // Adresse par défaut 0x18 pour ce capteur
      Serial.println("Failed to communicate with MPRLS sensor, check wiring?");
      lcd.clear();
       lcd.setCursor(0, 1);
       lcd.print("Error Com MPRLS");
      functionExit();
  }
  
  Serial.println("Found MPRLS sensor");
  lcd.setCursor(0, 1);
  lcd.print("Setup OK");
  delay(500);


  // Lecture de la pression depus le capteur
  pressure_hpa = mpr.readPressure();
  
  // INITIALISATION
  setLedRGB (255, 255, 0);
  lcd.clear();
  lcd.print(" INITIALISATION");
   lcd.setCursor(0, 1);
   lcd.print("****************");
  delay(2000);


  do {
    lcd.clear();
    lcd.print("SET low. point :");
     lcd.setCursor(0, 1);
     lowPoint = ((int)analogRead(PinPotentioL));
     lcd.print(lowPoint);
     lcd.print(" hPa");
    delay(100);
    if (debugMode > 0) {
      Serial.print("Valeure prise par lowPoint : ");
      Serial.println(lowPoint);
       Serial.print("Etat du bouton de validation : ");
       Serial.println(String(digitalRead(ButtonValidation)));
    }
  }
  while (digitalRead(ButtonValidation) == HIGH);
  delay(350); // Evite de passer la séquence si le bouton n'est pas relaché assez vite.
  
  do {
    lcd.clear();
    lcd.print("SET max. point :");
     lcd.setCursor(0, 1);
     maxPoint = ((int)analogRead(PinPotentioH));
     lcd.print(maxPoint);
     lcd.print(" hPa");
    delay(100);
    if (debugMode > 0) {
      Serial.print("Valeure prise par maxPoint : ");
      Serial.println(lowPoint);
       Serial.print("Etat du bouton de validation : ");
       Serial.println(String(digitalRead(ButtonValidation)));
    }
  }
  while(digitalRead(ButtonValidation) == HIGH);


}


void loop() {


  setLedRGB (0, 255, 0);


  // Affichage de la datas
  if (debugMode > 0) {
  Serial.print("Pression actuelle : ");
  Serial.print(pressure_hpa);
  Serial.println(" hPa");
  
  ValuePotentioH = (analogRead(PinPotentioH));
  Serial.print("Valeure prise par PotentioH :");
  Serial.println(ValuePotentioH);
  
  ValuePotentioL = (analogRead(PinPotentioL));
  Serial.print("Valeure prise par PotentioL :");
  Serial.println(ValuePotentioL);


  Serial.print("Etat du bouton de validation : ");
  Serial.println(String(digitalRead(ButtonValidation)));
  }


  lcd.clear();
   lcd.print("LET'S STARTED !!");
  delay(2000);
  lcd.clear();


  while (1) { // Boucle infinie
    int pressure_hpa = mpr.readPressure();
    lcd.setCursor(0, 0);
    lcd.print("hPa Actual: ");
    lcd.print(pressure_hpa);
    lcd.print(" "); // Efface le reste de la ligne


    if (pressure_hpa >= maxPoint) { // En fonction
      digitalWrite(LedAction, HIGH);
      digitalWrite(RelayMoteur, HIGH);
      lcd.setCursor(5, 1);
      lcd.print("Next : ");
      lcd.print(lowPoint);
      lcd.print("   ");
      delay(300);
    }
    else if (pressure_hpa <= lowPoint) { // En attente
      digitalWrite(LedAction, LOW);
      digitalWrite(RelayMoteur, LOW);
      lcd.setCursor(5, 1);
      lcd.print("Next : ");
      lcd.print(maxPoint);
      lcd.print("   ");
      delay(300);
    }
  }
}
